# Fritzing sketch schema (saved by Fritzing 0.9.3b)

parts:
  U1 = LIPO-1000mAh [package=lipo-1000]
  ESP1 = Firebeetle ESP32 IOT
  Bauteil1 = Adafruit LIS3DH [part_number="Adafruit #2809"]

nets:
  N1: U1.+, ESP1.Li-ion_+
  N2: U1.-, ESP1.Li-ion_-
  N3: ESP1.D4, Bauteil1.INT1
  N4: ESP1.SDA, Bauteil1.CS
  N5: ESP1.MISO, Bauteil1.SDO
  N6: ESP1.MOSI, Bauteil1.SDA
  N7: ESP1.SCK, Bauteil1.SCL
  GND: ESP1.GND, Bauteil1.GND
  3V3: ESP1.3V3, Bauteil1.VIN, Bauteil1.3.3V

custom parts:
  Adafruit LIS3DH: The LIS3DH is a very popular low power triple-axis accelerometer. It's low-cost, but has just about every 'extra' you'd want in an accelerometer: Three axis sensing, 10-bit precision ±2g/±4g/±8g/±16g selectable scaling Both I2C (2 possible addresses) and SPI interface options Interrupt output Multiple data rate options 1 Hz to 5Khz As low as 2uA current draw (just the chip itself, not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
